# Fritzing sketch motoca (saved by Fritzing 0.9.3b)
circuit board: 10cm x 5cm
perfboards: 1
stripboards: 4

parts:
  Arduino = Arduino Micro (Rev3)
  ParkSensor = male pin header, 4 pins [form="♂ (male)"]
  Siren = male pin header, 3 pins [form="♂ (male)"]
  Amp = female pin header, 4 pins [form="♀ (female)"]
  Power = male pin header, 2 pins [form="♂ (male)"]
  MicroSD = female pin header, 6 pins [form="♀ (female)"]
  S1 = male pin header, 2 pins [form="♂ (male)"]
  S2 = male pin header, 2 pins [form="♂ (male)"]
  S3 = male pin header, 2 pins [form="♂ (male)"]
  S4 = male pin header, 2 pins [form="♂ (male)"]

nets:
  N1: Arduino.MOSI, MicroSD.pin4
  N2: Arduino.GND, ParkSensor.pin4, Siren.pin3, Amp.pin1, Amp.pin2, Power.pin2, MicroSD.pin1, S1.pin1, S2.pin1, S3.pin1, S4.pin1
  N3: Arduino.D3/SCL, S4.pin2
  N4: Arduino.D4_PWM/A6, S3.pin2
  N5: Arduino.D5_PWM, S2.pin2
  N6: Arduino.D6_PWM/A7, S1.pin2
  N7: Arduino.D9_PWM/A9, Amp.pin3
  N8: Arduino.D10_PWM/A10, ParkSensor.pin2
  N9: Arduino.D11_PWM, ParkSensor.pin1
  N10: Arduino.D12_PWM/A11, Siren.pin1
  N11: Arduino.SCK, MicroSD.pin5
  N12: Arduino.MISO, MicroSD.pin3
  N13: Arduino.VIN, Power.pin1
  N14: Arduino.5V, ParkSensor.pin3, Siren.pin2, Amp.pin4, MicroSD.pin2
  N15: Arduino.A5, MicroSD.pin6
