# Fritzing sketch powertrain (saved by Fritzing 0.9.3b)

parts:
  Motor_6V = DC Motor
  Powertrain_power_line = DC Power [voltage=6V]
  Gearshift = SWITCH-DPDT [package=os]
  Throttle = Round Pushbutton
  D1 = Diode [package=diode-1n4148]
  Reverse_Signal = female pin header, 1 pin [form="♀ (female)"]

nets:
  N1: Motor_6V.pin_1, Throttle.leg1
  N2: Motor_6V.pin_2, Gearshift.1, Gearshift.6
  N3: Powertrain_power_line.V+, Gearshift.2
  N4: Powertrain_power_line.V-, Gearshift.5
  N5: Gearshift.3, Gearshift.4, Throttle.leg0, D1.C
  N6: D1.A, Reverse_Signal.pin1
